# Fritzing sketch LEDMatrixCircuit (saved by Fritzing 0.9.2b)
breadboards: 6

parts:
  Part1 = Arduino Uno (Rev3)
  Disp2 = LBT2088AH [part_number=LBT2088AH]
  Disp3 = LBT2088AH [part_number=LBT2088AH]
  Disp4 = LBT2088AH [part_number=LBT2088AH]
  U2 = 74HC595 [package="DIP16 [THT]"]
  U3 = 74HC595 [package="DIP16 [THT]"]
  U4 = 74HC595 [package="DIP16 [THT]"]
  U5 = 74HC595 [package="DIP16 [THT]"]
  R1 = Resistor [tolerance=±5% resistance=220 package=THT]
  R2 = Resistor [tolerance=±5% resistance=220 package=THT]
  R3 = Resistor [tolerance=±5% resistance=220 package=THT]
  R4 = Resistor [tolerance=±5% resistance=220 package=THT]
  R5 = Resistor [tolerance=±5% resistance=220 package=THT]
  R6 = Resistor [tolerance=±5% resistance=220 package=THT]
  R7 = Resistor [tolerance=±5% resistance=220 package=THT]
  R8 = Resistor [tolerance=±5% resistance=220 package=THT]
  U1 = 74HC595 [package="DIP16 [THT]"]
  R9 = Resistor [tolerance=±5% resistance=220 package=THT]
  R10 = Resistor [tolerance=±5% resistance=220 package=THT]
  R11 = Resistor [tolerance=±5% resistance=220 package=THT]
  R12 = Resistor [tolerance=±5% resistance=220 package=THT]
  R13 = Resistor [tolerance=±5% resistance=220 package=THT]
  R14 = Resistor [tolerance=±5% resistance=220 package=THT]
  R15 = Resistor [tolerance=±5% resistance=220 package=THT]
  R16 = Resistor [tolerance=±5% resistance=220 package=THT]
  R17 = Resistor [tolerance=±5% resistance=220 package=THT]
  R18 = Resistor [tolerance=±5% resistance=220 package=THT]
  R19 = Resistor [tolerance=±5% resistance=220 package=THT]
  R20 = Resistor [tolerance=±5% resistance=220 package=THT]
  R21 = Resistor [tolerance=±5% resistance=220 package=THT]
  R22 = Resistor [tolerance=±5% resistance=220 package=THT]
  R23 = Resistor [tolerance=±5% resistance=220 package=THT]
  R24 = Resistor [tolerance=±5% resistance=220 package=THT]
  R25 = Resistor [tolerance=±5% resistance=220 package=THT]
  R26 = Resistor [tolerance=±5% resistance=220 package=THT]
  R27 = Resistor [tolerance=±5% resistance=220 package=THT]
  R28 = Resistor [tolerance=±5% resistance=220 package=THT]
  R29 = Resistor [tolerance=±5% resistance=220 package=THT]
  R30 = Resistor [tolerance=±5% resistance=220 package=THT]
  R31 = Resistor [tolerance=±5% resistance=220 package=THT]
  R32 = Resistor [tolerance=±5% resistance=220 package=THT]
  Disp1 = LBT2088AH [part_number=LBT2088AH]

nets:
  N1: Part1.D11_PWM/MOSI, U2.SH_CP, U3.SH_CP, U4.SH_CP, U5.SH_CP, U1.SH_CP
  N2: Part1.D12/MISO, U2.ST_CP, U3.ST_CP, U4.ST_CP, U5.ST_CP, U1.ST_CP
  N3: Part1.D4, U1.DS
  VCC: Part1.5V, U2.MR, U2.VCC, U3.MR, U3.VCC, U4.MR, U4.VCC, U5.MR, U5.VCC, U1.MR, U1.VCC
  GND: Part1.GND, U2.GND, U3.GND, U4.GND, U5.GND, U1.GND
  N4: Disp2.pin1, Disp3.pin1, Disp4.pin1, U5.Q5, Disp1.pin1
  N5: Disp2.pin2, Disp3.pin2, Disp4.pin2, U5.Q6, Disp1.pin2
  N6: Disp2.pin_3, R9.Pin_1
  N7: Disp2.pin_4, R16.Pin_1
  N8: Disp2.pin_5, Disp3.pin_5, Disp4.pin_5, U5.Q7, Disp1.pin_5
  N9: Disp2.pin_6, R14.Pin_1
  N10: Disp2.pin_7, Disp3.pin_7, Disp4.pin_7, U5.Q4, Disp1.pin_7
  N11: Disp2.pin_8, Disp3.pin_8, Disp4.pin_8, U5.Q2, Disp1.pin_8
  N12: Disp2.pin_9, Disp3.pin_9, Disp4.pin_9, U5.Q0, Disp1.pin_9
  N13: Disp2.pin_10, R11.Pin_1
  N14: Disp2.pin_11, R15.Pin_1
  N15: Disp2.pin_12, Disp3.pin_12, Disp4.pin_12, U5.Q3, Disp1.pin_12
  N16: Disp2.pin_13, R12.Pin_1
  N17: Disp2.pin_14, Disp3.pin_14, Disp4.pin_14, U5.Q1, Disp1.pin_14
  N18: Disp2.pin_15, R13.Pin_1
  N19: Disp2.pin_16, R10.Pin_1
  N20: Disp3.pin_3, R17.Pin_1
  N21: Disp3.pin_4, R24.Pin_1
  N22: Disp3.pin_6, R22.Pin_1
  N23: Disp3.pin_10, R23.Pin_1
  N24: Disp3.pin_11, R19.Pin_1
  N25: Disp3.pin_13, R20.Pin_1
  N26: Disp3.pin_15, R21.Pin_1
  N27: Disp3.pin_16, R18.Pin_1
  N28: Disp4.pin_3, R25.Pin_1
  N29: Disp4.pin_4, R32.Pin_1
  N30: Disp4.pin_6, R30.Pin_1
  N31: Disp4.pin_10, R27.Pin_1
  N32: Disp4.pin_11, R31.Pin_1
  N33: Disp4.pin_13, R28.Pin_1
  N34: Disp4.pin_15, R29.Pin_1
  N35: Disp4.pin_16, R26.Pin_1
  N36: U2.Q1, R13.Pin_0
  N37: U2.Q2, R15.Pin_0
  N38: U2.Q3, R14.Pin_0
  N39: U2.Q4, R11.Pin_0
  N40: U2.Q5, R16.Pin_0
  N41: U2.Q6, R9.Pin_0
  N42: U2.Q7, R12.Pin_0
  N43: U2.Q7', U3.DS
  N44: U2.DS, U1.Q7'
  N45: U2.Q0, R10.Pin_0
  N46: U3.Q1, R21.Pin_0
  N47: U3.Q2, R23.Pin_0
  N48: U3.Q3, R22.Pin_0
  N49: U3.Q4, R19.Pin_0
  N50: U3.Q5, R24.Pin_0
  N51: U3.Q6, R17.Pin_0
  N52: U3.Q7, R20.Pin_0
  N53: U3.Q7', U4.DS
  N54: U3.Q0, R18.Pin_0
  N55: U4.Q1, R29.Pin_0
  N56: U4.Q2, R31.Pin_0
  N57: U4.Q3, R30.Pin_0
  N58: U4.Q4, R27.Pin_0
  N59: U4.Q5, R32.Pin_0
  N60: U4.Q6, R25.Pin_0
  N61: U4.Q7, R28.Pin_0
  N62: U4.Q7', U5.DS
  N63: U4.Q0, R26.Pin_0
  N64: R1.Pin_0, U1.Q0
  N65: R1.Pin_1, Disp1.pin_16
  N66: R2.Pin_0, U1.Q1
  N67: R2.Pin_1, Disp1.pin_15
  N68: R3.Pin_0, U1.Q2
  N69: R3.Pin_1, Disp1.pin_10
  N70: R4.Pin_0, U1.Q3
  N71: R4.Pin_1, Disp1.pin_6
  N72: R5.Pin_0, U1.Q4
  N73: R5.Pin_1, Disp1.pin_11
  N74: R6.Pin_0, U1.Q5
  N75: R6.Pin_1, Disp1.pin_4
  N76: R7.Pin_0, U1.Q6
  N77: R7.Pin_1, Disp1.pin_3
  N78: R8.Pin_0, U1.Q7
  N79: R8.Pin_1, Disp1.pin_13

// code stored in the sketch: ArduinoSketch_MatrixLED.ino
/**
 * Copyright (c) 2015 Hong Quach and Norah Alballa
 *
 * This source file is licensed under the "MIT License." Please see the LICENSE
 * in this distribution for license terms.
 *
 * Matrix rendering controlled by serial
 * Send each frame through the serial port (64 bytes buffer size)
 * marked with the startChar and end with the endChar.
 *
 */

String inputString = "";         // a string to hold incoming data
boolean stringComplete = false;  // whether the string is complete
char startChar = '^';            // char to indicate the start of matrix data
char endChar = '$';              // char to indicate the end of the matrix data
boolean dataStarted = false;     // signal that matrix data is comming in

// Initial frame
String matrixData = "ff00ff0000ff00ffff00ff0000ff00ffff00ff0000ff00ffff00ff0000ff00ff";
String newMatrixData = "";

boolean enableDebug = false;
int matrixWidth = 32;
int matrixHeight = 8;
int serialSpeed = 9600;

//Pin connected to latch pin #12 (ST_CP) of 74HC595
const int latchPin = 12;
//Pin connected to clock pin #11 (SH_CP) of 74HC595
const int clockPin = 11;
//Pin connected to Data pin #14 (DS) of 74HC595
const int dataPin = 4;
//Pin connect to LED for visual feedback for debug purpose
const int ledPin = 13;

/**
 * Arduino init function
 */
void setup() {
  //set pins to output because they are addressed in the main loop
  pinMode(latchPin, OUTPUT);
  pinMode(dataPin, OUTPUT);
  pinMode(clockPin, OUTPUT);
  Serial.begin(serialSpeed);
  Serial.print("Starting Listing on Serial Port.  ");
  Serial.println("Use '^' to start a new data and '$' to terminate.");
  // reserve 200 bytes for strings:
  matrixData.reserve(200);
  newMatrixData.reserve(200);
  //TODO:  Send out the startChar, endChar, matrix Width and Height to the Host
}

/**
 * Recieve chars from serial port
 */
void getSerialInput() {
  for (int i = 0; i < 66; i++) {
    if (Serial.available()) {
      char inChar = (char)Serial.read();
      if (inChar == startChar && !dataStarted) {
        if (enableDebug) {
          digitalWrite(ledPin, true);
          Serial.println("Start char detected");
        }
        newMatrixData = "";
        dataStarted = true;
      }
      else if (inChar == endChar && dataStarted) {
        if (enableDebug) {
          Serial.println("End   char detected");
        }
        if (newMatrixData == "^enableDebug^") {
          enableDebug = true;
        }
        else if (newMatrixData == "^disableDebug^") {
          enableDebug = false;
        }
        else {
          matrixData = newMatrixData;
          dataStarted = false;
        }
        if (enableDebug) {
          digitalWrite(ledPin, false);
          Serial.print("New Frame:  ");
          Serial.println(matrixData);
        }
      }
      else if (dataStarted) {
        newMatrixData += inChar;
      }
    }
    else {
      break;
    }
  }
}

/**
 * The 'main' of Arduino
 */
void loop() {
  getSerialInput();
  render(matrixData, 1);
}

/**
 * Render each frame
 */
void render(String frame, int holdCycle) {
  int registerCount = 5;
  int layerCount = 8;
  byte registers[registerCount];
  for (int h = 0; h < holdCycle; h++) {
    unsigned layerBit = 1;
    for (int layer = 0; layer < layerCount; layer++) {
      // Lines up the bits to be shipped to the register
      int subFrameIndex = layer * layerCount;
      registers[0] = byte(layerBit);
      for (int r = 1; r < registerCount; r++)
      {
        registers[r] = hexStringToByte(frame.substring(subFrameIndex + ((r - 1) * 2), subFrameIndex + (r * 2)));
      }
      shiftOutToRegisters(registerCount, registers);

      //Next layer
      layerBit = (layerBit << 1);
    }
  }
}

/**
 * shifting one byte per register (74HC595) wired in series.
 */
void shiftOutToRegisters(int registerCount, byte* registers) {
  // turn off the output so the pins don't light up
  // while you're shifting bits:
  digitalWrite(latchPin, LOW);
  for (int i = 0; i < registerCount; i++) {
    shiftOut(dataPin, clockPin, MSBFIRST, registers[i]);
  }
  // turn on the output so the LEDs can light up:
  digitalWrite(latchPin, HIGH);
}

/**
 * Convert a string in HEX to a byte
 */
byte hexStringToByte(String hexString) {
  byte temp = 0;
  int input_len = hexString.length();
  hexString.toUpperCase();
  for (int i = 0; i < input_len; i++) {
    int int_of_char = int(hexString[i]);
    int int_of_0 = int('0');
    int int_of_A = int('A');
    int char_value = 0;
    if (int_of_char >= int_of_0 && int_of_char <= int_of_0 + 9) {
      char_value = int_of_char - int_of_0;
    } else if (int_of_char >= int_of_A && int_of_char <= int_of_A + 5) {
      char_value = int_of_char - int_of_A + 10;
    }
    temp |= (char_value << ((input_len - 1 - i) * 4));
  }
  return temp;
}
